# Fritzing sketch felisha_stretcher_incomplete (saved by Fritzing 0.9.9b)
breadboards: 1

parts:
  Part1 = Arduino Uno (Rev3)
  R1 = Rotary Potentiometer (Small) [maximum_resistance=100kΩ package=THT]
  J1 = Basic Servo
  J2 = Basic Servo
  J3 = Basic Servo
  J4 = Basic Servo
  BAT1 = BC9VPC [package=bc9vpc]  # not connected
  Power_plug1 = Power plug

nets:
  N1: Part1.A0, R1.wiper
  N2: Part1.D3_PWM, J3.pulse, J4.pulse
  N3: Part1.D5_PWM, J1.pulse, J2.pulse
  N4: Part1.5V, R1.leg1
  GND: Part1.GND, R1.leg2, J1.gnd, J2.gnd, J3.gnd, J4.gnd, Power_plug1.GND
  VCC: J1.vcc, J2.vcc, J3.vcc, J4.vcc, Power_plug1.VCC

notes:
  *****WIRE COLOR KEY*****
  red = power
  black = ground
  blue = input analog signal
  yellow = output analog signal
  + arduino is powered by 9V battery connected by terminal clip deal to dc input jack (to arduino) dc input jack??? need to investiagte, remember something about power outiside and ground inside or visa versa
  + all servos are connected to the same power module board, with a wall power (9V 3A) input and a 5V unkown output of current from the power module board
  The power output of this board is connected to the same bread board row as all the servo power cable, the ground is tied into the 'common ground'
